// Logisim project onecpcpu.circ as structural Verilog: 13 circuits, main circuit main
module main (
  input  in_1,
  output [31:0] out_2,
  output out_3,
  output [4:0] out_4,
  output [31:0] out_5,
  output out_6,
  output [4:0] out_7,
  output [31:0] out_8
);

  wire Alusrc, clk, Extw, Memread, Memtoreg, Regdst, whbeq, WhExt, zero;
  wire [1:0] aluop;
  wire [31:0] r1, r3, r22, r23, re;

  IFU IFU (.whbeq(whbeq), .zero(zero), .clk(clk), .Reset(in_1), .Input(out_2));
  Multiplexer #(.width(5)) multiplexer_1 (.in0(out_2[20:16]), .in1(out_2[15:11]), .out(out_4), .sel(Regdst), .en(1'b1));
  GRF GRF (
    .clk(clk), .Reset(in_1), .Regwrite(out_3), .wd(out_4), .account(out_5), .rd1(out_2[25:21]),
    .rd2(out_2[20:16]), .r1(r1), .r2(out_8));
  Controller Controller (
    .in_1(out_2[5]), .in_2(out_2[4]), .in_3(out_2[3]), .in_4(out_2[2]), .in_5(out_2[1]), .in_6(out_2[0]),
    .in_7(out_2[31]), .in_8(out_2[30]), .in_9(out_2[29]), .in_10(out_2[28]), .in_11(out_2[27]),
    .in_12(out_2[26]), .out_13(Regdst), .out_14(Alusrc), .out_15(out_3), .out_16(out_6), .out_17(Memread),
    .out_18(whbeq), .out_19(Memtoreg), .out_20(WhExt), .out_21(Extw), .out_22(aluop));
  EXT EXT (.Input(out_2[15:0]), .EXTop1(Extw), .EXTop2(WhExt), .Output(r22));
  Multiplexer #(.width(32)) multiplexer_2 (.in0(out_8), .in1(r22), .out(r23), .sel(Alusrc), .en(1'b1));
  ALU ALU (.in_1(r1), .in_2(r23), .in_3(aluop), .out_4({re[31:7], out_7, re[1:0]}), .out_5(zero));
  Multiplexer #(.width(32)) multiplexer_3 (
    .in0({re[31:7], out_7, re[1:0]}), .in1(r3), .out(out_5), .sel(Memtoreg), .en(1'b1));
  Clock clock_1 (.out(clk));
  DM DM (.memaddr(out_7), .\input (out_8), .memwrite(out_6), .clk(clk), .reset(in_1), .out_6(r3));

  // Other names for the same wires on the sheet: func[5:0] = out_2[5:0]; imm16[15:0] = out_2[15:0];
  //   Instr[31:0] = out_2; shamt[4:0] = out_2[10:6]; rd[4:0] = out_2[15:11]; rt[4:0] = out_2[20:16];
  //   rs[4:0] = out_2[25:21]; op[5:0] = out_2[31:26]; Memwrite = out_6; r21[31:0] = out_8; MemAddr[4:0] = out_7;
  //   re[6:2] = out_7; RegAddr[4:0] = out_4; Regwrite = out_3; Reset = in_1; rl[31:0] = out_5
endmodule

module IFU (
  input  whbeq,
  input  zero,
  input  clk,
  input  Reset,
  output [31:0] Input
);

  wire and_1_out;
  wire [31:0] bit_extender_1_out, multiplexer_1_out, n32add_1_out_3, n32add_2_out_3, pc;

  and and_1 (and_1_out, whbeq, zero);
  _32add u_32add_1 (.in_1(pc), .in_2(32'h1), .out_3(n32add_1_out_3));
  assign bit_extender_1_out = {{16{Input[15]}}, Input[15:0]};  // Bit_Extender bit_extender_1
  _32add u_32add_2 (.in_1(n32add_1_out_3), .in_2(bit_extender_1_out), .out_3(n32add_2_out_3));
  Multiplexer #(.width(32)) multiplexer_1 (
    .in0(n32add_1_out_3), .in1(n32add_2_out_3), .out(multiplexer_1_out), .sel(and_1_out), .en(1'b1));
  Register #(.width(32)) register_1 (.D(multiplexer_1_out), .Q(pc), .clk(clk), .clr(Reset));  // open: en
  ROM #(.addrWidth(5), .dataWidth(32)) rom_1 (.addr(pc[4:0]), .data(Input));  // open: sel

  // Other names for the same wires on the sheet: dai[31:0] = Input

  // Notes on the sheet:
  //   contents of rom_1 (hex, n*v repeats v):
  //   341c0000 341d0000 340080f8 36ee0367 3593769c 34dda539 3465c5dc 34be0ff1 3472af1d 35566602 35fe72a7
  //   3437ff23 37b9649e 3690bf9b 37fe4e0c 3711f49d 3c113bfe 3c057433 3c03c451 3c04c431 3c1c24d9 3c1bf0da
  //   3c0ccc68 3c0a118d 3c1021ea 3c0004d3 3c16115b 3c184f06 3c1215de 1000ffff
endmodule

module GRF (
  input  clk,
  input  Reset,
  input  Regwrite,
  input  [4:0] wd,
  input  [31:0] account,
  input  [4:0] rd1,
  input  [4:0] rd2,
  output [31:0] r1,
  output [31:0] r2
);

  wire decoder_1_out0, decoder_1_out1, decoder_1_out2, decoder_1_out3, decoder_1_out4, decoder_1_out5,
       decoder_1_out6, decoder_1_out7, decoder_1_out8, decoder_1_out9, decoder_1_out10, decoder_1_out11,
       decoder_1_out12, decoder_1_out13, decoder_1_out14, decoder_1_out15, decoder_1_out16, decoder_1_out17,
       decoder_1_out18, decoder_1_out19, decoder_1_out20, decoder_1_out21, decoder_1_out22, decoder_1_out23,
       decoder_1_out24, decoder_1_out25, decoder_1_out26, decoder_1_out27, decoder_1_out28, decoder_1_out29,
       decoder_1_out30, decoder_1_out31;
  wire [31:0] _0_q, _1_q, _2_q, _3_q, _4_q, _5_q, _6_q, _7_q, _8_q, _9_q, _10_q, _11_q, _12_q, _13_q, _14_q,
       _15_q, _16_q, _17_q, _18_q, _19_q, _20_q, _21_q, _22_q, _23_q, _24_q, _25_q, _26_q, _27_q, _28_q,
       _29_q, _30_q, _31_q;

  Decoder #(.select(5), .disabled(0)) decoder_1 (
    .out0(decoder_1_out0), .out1(decoder_1_out1), .out2(decoder_1_out2), .out3(decoder_1_out3),
    .out4(decoder_1_out4), .out5(decoder_1_out5), .out6(decoder_1_out6), .out7(decoder_1_out7),
    .out8(decoder_1_out8), .out9(decoder_1_out9), .out10(decoder_1_out10), .out11(decoder_1_out11),
    .out12(decoder_1_out12), .out13(decoder_1_out13), .out14(decoder_1_out14), .out15(decoder_1_out15),
    .out16(decoder_1_out16), .out17(decoder_1_out17), .out18(decoder_1_out18), .out19(decoder_1_out19),
    .out20(decoder_1_out20), .out21(decoder_1_out21), .out22(decoder_1_out22), .out23(decoder_1_out23),
    .out24(decoder_1_out24), .out25(decoder_1_out25), .out26(decoder_1_out26), .out27(decoder_1_out27),
    .out28(decoder_1_out28), .out29(decoder_1_out29), .out30(decoder_1_out30), .out31(decoder_1_out31),
    .sel(wd), .en(Regwrite));
  Register #(.width(32)) _0 (.D(account), .en(decoder_1_out0), .Q(_0_q), .clk(clk), .clr(1'b1));
  Register #(.width(32)) _1 (.D(account), .en(decoder_1_out1), .Q(_1_q), .clk(clk), .clr(Reset));
  Register #(.width(32)) _2 (.D(account), .en(decoder_1_out2), .Q(_2_q), .clk(clk), .clr(Reset));
  Register #(.width(32)) _3 (.D(account), .en(decoder_1_out3), .Q(_3_q), .clk(clk), .clr(Reset));
  Register #(.width(32)) _4 (.D(account), .en(decoder_1_out4), .Q(_4_q), .clk(clk), .clr(Reset));
  Register #(.width(32)) _5 (.D(account), .en(decoder_1_out5), .Q(_5_q), .clk(clk), .clr(Reset));
  Register #(.width(32)) _6 (.D(account), .en(decoder_1_out6), .Q(_6_q), .clk(clk), .clr(Reset));
  Register #(.width(32)) _7 (.D(account), .en(decoder_1_out7), .Q(_7_q), .clk(clk), .clr(Reset));
  Register #(.width(32)) _8 (.D(account), .en(decoder_1_out8), .Q(_8_q), .clk(clk), .clr(Reset));
  Register #(.width(32)) _9 (.D(account), .en(decoder_1_out9), .Q(_9_q), .clk(clk), .clr(Reset));
  Register #(.width(32)) _10 (.D(account), .en(decoder_1_out10), .Q(_10_q), .clk(clk), .clr(Reset));
  Register #(.width(32)) _11 (.D(account), .en(decoder_1_out11), .Q(_11_q), .clk(clk), .clr(Reset));
  Register #(.width(32)) _12 (.D(account), .en(decoder_1_out12), .Q(_12_q), .clk(clk), .clr(Reset));
  Register #(.width(32)) _13 (.D(account), .en(decoder_1_out13), .Q(_13_q), .clk(clk), .clr(Reset));
  Register #(.width(32)) _14 (.D(account), .en(decoder_1_out14), .Q(_14_q), .clk(clk), .clr(Reset));
  Register #(.width(32)) _15 (.D(account), .en(decoder_1_out15), .Q(_15_q), .clk(clk), .clr(Reset));
  Register #(.width(32)) _16 (.D(account), .en(decoder_1_out16), .Q(_16_q), .clk(clk), .clr(Reset));
  Register #(.width(32)) _17 (.D(account), .en(decoder_1_out17), .Q(_17_q), .clk(clk), .clr(Reset));
  Register #(.width(32)) _18 (.D(account), .en(decoder_1_out18), .Q(_18_q), .clk(clk), .clr(Reset));
  Register #(.width(32)) _19 (.D(account), .en(decoder_1_out19), .Q(_19_q), .clk(clk), .clr(Reset));
  Register #(.width(32)) _20 (.D(account), .en(decoder_1_out20), .Q(_20_q), .clk(clk), .clr(Reset));
  Register #(.width(32)) _21 (.D(account), .en(decoder_1_out21), .Q(_21_q), .clk(clk), .clr(Reset));
  Register #(.width(32)) _22 (.D(account), .en(decoder_1_out22), .Q(_22_q), .clk(clk), .clr(Reset));
  Register #(.width(32)) _23 (.D(account), .en(decoder_1_out23), .Q(_23_q), .clk(clk), .clr(Reset));
  Register #(.width(32)) _24 (.D(account), .en(decoder_1_out24), .Q(_24_q), .clk(clk), .clr(Reset));
  Register #(.width(32)) _25 (.D(account), .en(decoder_1_out25), .Q(_25_q), .clk(clk), .clr(Reset));
  Register #(.width(32)) _26 (.D(account), .en(decoder_1_out26), .Q(_26_q), .clk(clk), .clr(Reset));
  Register #(.width(32)) _27 (.D(account), .en(decoder_1_out27), .Q(_27_q), .clk(clk), .clr(Reset));
  Register #(.width(32)) _28 (.D(account), .en(decoder_1_out28), .Q(_28_q), .clk(clk), .clr(Reset));
  Register #(.width(32)) _29 (.D(account), .en(decoder_1_out29), .Q(_29_q), .clk(clk), .clr(Reset));
  Register #(.width(32)) _30 (.D(account), .en(decoder_1_out30), .Q(_30_q), .clk(clk), .clr(Reset));
  Register #(.width(32)) _31 (.D(account), .en(decoder_1_out31), .Q(_31_q), .clk(clk), .clr(Reset));
  Multiplexer #(.select(5), .width(32)) multiplexer_1 (
    .in0(_0_q), .in1(_1_q), .in2(_2_q), .in3(_3_q), .in4(_4_q), .in5(_5_q), .in6(_6_q), .in7(_7_q),
    .in8(_8_q), .in9(_9_q), .in10(_10_q), .in11(_11_q), .in12(_12_q), .in13(_13_q), .in14(_14_q),
    .in15(_15_q), .in16(_16_q), .in17(_17_q), .in18(_18_q), .in19(_19_q), .in20(_20_q), .in21(_21_q),
    .in22(_22_q), .in23(_23_q), .in24(_24_q), .in25(_25_q), .in26(_26_q), .in27(_27_q), .in28(_28_q),
    .in29(_29_q), .in30(_30_q), .in31(_31_q), .out(r1), .sel(rd1), .en(1'b1));
  Multiplexer #(.select(5), .width(32)) multiplexer_2 (
    .in0(_0_q), .in1(_1_q), .in2(_2_q), .in3(_3_q), .in4(_4_q), .in5(_5_q), .in6(_6_q), .in7(_7_q),
    .in8(_8_q), .in9(_9_q), .in10(_10_q), .in11(_11_q), .in12(_12_q), .in13(_13_q), .in14(_14_q),
    .in15(_15_q), .in16(_16_q), .in17(_17_q), .in18(_18_q), .in19(_19_q), .in20(_20_q), .in21(_21_q),
    .in22(_22_q), .in23(_23_q), .in24(_24_q), .in25(_25_q), .in26(_26_q), .in27(_27_q), .in28(_28_q),
    .in29(_29_q), .in30(_30_q), .in31(_31_q), .out(r2), .sel(rd2), .en(1'b1));
endmodule

module ALU (
  input  [31:0] in_1,
  input  [31:0] in_2,
  input  [1:0] in_3,
  output [31:0] out_4,
  output out_5
);

  wire [31:0] n32add_1_out_3, n32sub_1_out_3, or_1_out;

  _32add u_32add_1 (.in_1(in_1), .in_2(in_2), .out_3(n32add_1_out_3));
  _32sub u_32sub_1 (.in_1(in_1), .in_2(in_2), .out_3(n32sub_1_out_3));
  assign or_1_out = in_1 | in_2;  // OR_Gate or_1, 32 bits wide
  Comparator #(.width(32), .mode("unsigned")) comparator_1 (.a(in_1), .b(in_2), .eq(out_5));  // open: gt, lt
  Multiplexer #(.select(2), .width(32)) multiplexer_1 (
    .in0(n32add_1_out_3), .in1(n32sub_1_out_3), .in2(or_1_out), .out(out_4), .sel(in_3), .en(1'b1));  // open: in3
endmodule

module _1add (
  input  A,
  input  B,
  input  C,
  output O,
  output OV
);

  wire and_1_out, and_2_out, and_3_out, and_4_out, and_5_out, and_6_out, and_7_out, not_1_out, not_2_out,
       not_3_out, not_4_out, not_5_out, not_6_out;

  not not_1 (not_1_out, A);
  not not_2 (not_2_out, B);
  not not_3 (not_3_out, A);
  not not_4 (not_4_out, C);
  not not_5 (not_5_out, B);
  not not_6 (not_6_out, C);
  and and_1 (and_1_out, B, C);
  and and_2 (and_2_out, A, C);
  and and_3 (and_3_out, A, B);
  and and_4 (and_4_out, not_1_out, not_2_out, C);
  and and_5 (and_5_out, not_3_out, B, not_4_out);
  and and_6 (and_6_out, A, not_5_out, not_6_out);
  and and_7 (and_7_out, A, B, C);
  or or_1 (OV, and_1_out, and_2_out, and_3_out);
  or or_2 (O, and_4_out, and_5_out, and_6_out, and_7_out);
endmodule

module _32add (
  input  [31:0] in_1,
  input  [31:0] in_2,
  output [31:0] out_3
);

  wire n8add_1_out_5, n8add_2_out_5, n8add_3_out_5;

  _8add u_8add_1 (.in_1(in_1[7:0]), .in_2(in_2[7:0]), .in_3(1'b0), .out_4(out_3[7:0]), .out_5(n8add_1_out_5));
  _8add u_8add_2 (
    .in_1(in_1[15:8]), .in_2(in_2[15:8]), .in_3(n8add_1_out_5), .out_4(out_3[15:8]), .out_5(n8add_2_out_5));
  _8add u_8add_3 (
    .in_1(in_1[23:16]), .in_2(in_2[23:16]), .in_3(n8add_2_out_5), .out_4(out_3[23:16]), .out_5(n8add_3_out_5));
  _8add u_8add_4 (.in_1(in_1[31:24]), .in_2(in_2[31:24]), .in_3(n8add_3_out_5), .out_4(out_3[31:24]));  // open: out_5
endmodule

module _8add (
  input  [7:0] in_1,
  input  [7:0] in_2,
  input  in_3,
  output [7:0] out_4,
  output out_5
);

  wire n1add_1_ov, n1add_2_ov, n1add_3_ov, n1add_4_ov, n1add_5_ov, n1add_6_ov, n1add_7_ov;

  _1add u_1add_1 (.A(in_1[0]), .B(in_2[0]), .C(in_3), .O(out_4[0]), .OV(n1add_1_ov));
  _1add u_1add_2 (.A(in_1[2]), .B(in_2[2]), .C(n1add_5_ov), .O(out_4[2]), .OV(n1add_2_ov));
  _1add u_1add_3 (.A(in_1[4]), .B(in_2[4]), .C(n1add_6_ov), .O(out_4[4]), .OV(n1add_3_ov));
  _1add u_1add_4 (.A(in_1[6]), .B(in_2[6]), .C(n1add_7_ov), .O(out_4[6]), .OV(n1add_4_ov));
  _1add u_1add_5 (.A(in_1[1]), .B(in_2[1]), .C(n1add_1_ov), .O(out_4[1]), .OV(n1add_5_ov));
  _1add u_1add_6 (.A(in_1[3]), .B(in_2[3]), .C(n1add_2_ov), .O(out_4[3]), .OV(n1add_6_ov));
  _1add u_1add_7 (.A(in_1[5]), .B(in_2[5]), .C(n1add_3_ov), .O(out_4[5]), .OV(n1add_7_ov));
  _1add u_1add_8 (.A(in_1[7]), .B(in_2[7]), .C(n1add_4_ov), .O(out_4[7]), .OV(out_5));
endmodule

module _1sub (
  input  A,
  input  B,
  input  C,
  output O,
  output Ov
);

  wire and_1_out, and_2_out, and_3_out, and_4_out, and_5_out, and_6_out, and_7_out, not_1_out, not_2_out,
       not_3_out, not_4_out, not_5_out, not_6_out, not_7_out, not_8_out;

  not not_1 (not_1_out, A);
  not not_2 (not_2_out, B);
  not not_3 (not_3_out, A);
  not not_4 (not_4_out, C);
  not not_5 (not_5_out, B);
  not not_6 (not_6_out, C);
  not not_7 (not_7_out, A);
  not not_8 (not_8_out, A);
  and and_1 (and_1_out, not_1_out, not_2_out, C);
  and and_2 (and_2_out, not_3_out, B, not_4_out);
  and and_3 (and_3_out, A, not_5_out, not_6_out);
  and and_4 (and_4_out, A, B, C);
  and and_5 (and_5_out, not_7_out, C);
  and and_6 (and_6_out, not_8_out, B);
  and and_7 (and_7_out, B, C);
  or or_1 (O, and_1_out, and_2_out, and_3_out, and_4_out);
  or or_2 (Ov, and_5_out, and_6_out, and_7_out);
endmodule

module _8sub (
  input  [7:0] in_1,
  input  [7:0] in_2,
  input  in_3,
  output [7:0] out_4,
  output out_5
);

  wire n1sub_1_ov, n1sub_2_ov, n1sub_3_ov, n1sub_4_ov, n1sub_5_ov, n1sub_6_ov, n1sub_7_ov;

  _1sub u_1sub_1 (.A(in_1[0]), .B(in_2[0]), .C(in_3), .O(out_4[0]), .Ov(n1sub_1_ov));
  _1sub u_1sub_2 (.A(in_1[2]), .B(in_2[2]), .C(n1sub_5_ov), .O(out_4[2]), .Ov(n1sub_2_ov));
  _1sub u_1sub_3 (.A(in_1[4]), .B(in_2[4]), .C(n1sub_6_ov), .O(out_4[4]), .Ov(n1sub_3_ov));
  _1sub u_1sub_4 (.A(in_1[6]), .B(in_2[6]), .C(n1sub_7_ov), .O(out_4[6]), .Ov(n1sub_4_ov));
  _1sub u_1sub_5 (.A(in_1[1]), .B(in_2[1]), .C(n1sub_1_ov), .O(out_4[1]), .Ov(n1sub_5_ov));
  _1sub u_1sub_6 (.A(in_1[3]), .B(in_2[3]), .C(n1sub_2_ov), .O(out_4[3]), .Ov(n1sub_6_ov));
  _1sub u_1sub_7 (.A(in_1[5]), .B(in_2[5]), .C(n1sub_3_ov), .O(out_4[5]), .Ov(n1sub_7_ov));
  _1sub u_1sub_8 (.A(in_1[7]), .B(in_2[7]), .C(n1sub_4_ov), .O(out_4[7]), .Ov(out_5));
endmodule

module _32sub (
  input  [31:0] in_1,
  input  [31:0] in_2,
  output [31:0] out_3
);

  wire n8sub_1_out_5, n8sub_2_out_5, n8sub_3_out_5;

  _8sub u_8sub_1 (.in_1(in_1[7:0]), .in_2(in_2[7:0]), .in_3(1'b0), .out_4(out_3[7:0]), .out_5(n8sub_1_out_5));
  _8sub u_8sub_2 (
    .in_1(in_1[15:8]), .in_2(in_2[15:8]), .in_3(n8sub_1_out_5), .out_4(out_3[15:8]), .out_5(n8sub_2_out_5));
  _8sub u_8sub_3 (
    .in_1(in_1[23:16]), .in_2(in_2[23:16]), .in_3(n8sub_2_out_5), .out_4(out_3[23:16]), .out_5(n8sub_3_out_5));
  _8sub u_8sub_4 (.in_1(in_1[31:24]), .in_2(in_2[31:24]), .in_3(n8sub_3_out_5), .out_4(out_3[31:24]));  // open: out_5
endmodule

module DM (
  input  [4:0] memaddr,
  input  [31:0] \input ,
  input  memwrite,
  input  clk,
  input  reset,
  output [31:0] out_6
);

  RAM #(.addrWidth(5), .dataWidth(32), .bus("separate")) ram_1 (
    .addr(memaddr), .din(\input ), .data(out_6), .str(memwrite), .clk(clk), .clr(reset));  // open: sel, ld
endmodule

module EXT (
  input  [15:0] Input,
  input  EXTop1,
  input  EXTop2,
  output [31:0] Output
);

  wire [31:0] bit_extender_1_out, bit_extender_2_out, multiplexer_1_out;

  assign bit_extender_1_out = {{16{Input[15]}}, Input};  // Bit_Extender bit_extender_1
  assign bit_extender_2_out = {{16{1'b0}}, Input};  // Bit_Extender bit_extender_2
  Multiplexer #(.width(32), .disabled(0)) multiplexer_1 (
    .in0({Input, {16{1'b0}}}), .in1(bit_extender_2_out), .out(multiplexer_1_out), .sel(EXTop1), .en(1'b1));
  Multiplexer #(.width(32), .disabled(0)) multiplexer_2 (
    .in0(multiplexer_1_out), .in1(bit_extender_1_out), .out(Output), .sel(EXTop2), .en(1'b1));
endmodule

module Controller (
  input  in_1,
  input  in_2,
  input  in_3,
  input  in_4,
  input  in_5,
  input  in_6,
  input  in_7,
  input  in_8,
  input  in_9,
  input  in_10,
  input  in_11,
  input  in_12,
  output out_13,
  output out_14,
  output out_15,
  output out_16,
  output out_17,
  output out_18,
  output out_19,
  output out_20,
  output out_21,
  output [1:0] out_22
);

  wire addu_out, beq_out, lui_out, lw_out, sw_out;

  and addu (addu_out, in_1, ~in_2, ~in_3, ~in_4, ~in_5, in_6, ~in_7, ~in_8, ~in_9, ~in_10, ~in_11, ~in_12);  // AND_Gate
  and subu (out_22[0], in_1, ~in_2, ~in_3, ~in_4, in_5, in_6, ~in_7, ~in_8, ~in_9, ~in_10, ~in_11, ~in_12);  // AND_Gate
  and ori (out_22[1], ~in_7, ~in_8, in_9, in_10, ~in_11, in_12);  // AND_Gate
  and lw (lw_out, in_7, ~in_8, ~in_9, ~in_10, in_11, in_12);  // AND_Gate
  and sw (sw_out, in_7, ~in_8, in_9, ~in_10, in_11, in_12);  // AND_Gate
  and beq (beq_out, ~in_7, ~in_8, ~in_9, in_10, ~in_11, ~in_12);  // AND_Gate
  and lui (lui_out, ~in_7, ~in_8, in_9, in_10, in_11, in_12);  // AND_Gate
  or Regdet (out_13, addu_out, out_22[0]);
  or Alusrc (out_14, out_22[1], lw_out, sw_out, lui_out);
  or Regwrite (out_15, addu_out, out_22[0], out_22[1], lw_out, lui_out);
  buf Memwrite (out_16, sw_out);  // OR_Gate
  buf Memread (out_17, lw_out);  // OR_Gate
  buf Pc (out_18, beq_out);  // OR_Gate
  buf Memtoreg (out_19, lw_out);  // OR_Gate
  or Whext (out_20, lw_out, sw_out);
  buf Ex_g (out_21, out_22[1]);  // OR_Gate
endmodule
